# Fritzing sketch tutorial (saved by Fritzing 1.0.5)
breadboards: 1

parts:
  LED1 = RGB LED (com. cathode, rgb) [color="Red (633nm)" current=0.030A package="5 mm [THT]"]
  S1 = Toggle Switch [package=THT]
  R1 = Resistor [tolerance=±5% power=0.25W resistance=220 package=THT]
  S2 = Pushbutton [package="[THT]"]
  S3 = Pushbutton [package="[THT]"]
  R2 = Resistor [tolerance=±5% power=0.25W resistance=220 package=THT]
  VCC1 = Battery [internal_resistance=0.1Ω]

nets:
  N1: LED1.common_cathode, S2.Pin_1, S2.Pin_2
  N2: LED1.green_anode, VCC1.-
  N3: LED1.blue_anode, S1.L1
  N4: S1.COM, R1.Pin_1
  N5: R1.Pin_0, R2.Pin_0, VCC1.+
  N6: S2.Pin_3, S2.Pin_4, R2.Pin_1
  N7: S3.Pin_1, S3.Pin_2
  N8: S3.Pin_3, S3.Pin_4
