# Fritzing sketch ultrasonic (saved by Fritzing 1.0.5)
breadboards: 1

parts:
  A1 = ESP32 DevKitc V4
  HC-SR04_Sensor_1 = HC-SR04 Ultrasonic Distance Sensor
  LED1 = LED - 5mm [color="Blue (470nm)" current=0.030A package="5 mm [THT]"]
  R1 = Resistor [tolerance=±5% power=0.25W resistance=220 package=THT]
  R2 = Resistor [tolerance=±5% power=0.25W resistance=220 package=THT]  # not connected
  LED2 = LED - 5mm [color="Blue (470nm)" current=0.030A package="5 mm [THT]"]
  R3 = Resistor [tolerance=±5% power=0.25W resistance=220 package=THT]
  LED3 = LED - 5mm [color="Blue (470nm)" current=0.030A package="5 mm [THT]"]
  R4 = Resistor [tolerance=±5% power=0.25W resistance=220 package=THT]
  LED4 = LED - 5mm [color="Blue (470nm)" current=0.030A package="5 mm [THT]"]
  R5 = Resistor [tolerance=±5% power=0.25W resistance=220 package=THT]  # not connected
  LED5 = LED - 5mm [color="Blue (470nm)" current=0.030A package="5 mm [THT]"]
  R6 = Resistor [tolerance=±5% power=0.25W resistance=220 package=THT]
  LED6 = LED - 5mm [color="Blue (470nm)" current=0.030A package="5 mm [THT]"]
  R7 = Resistor [tolerance=±5% power=0.25W resistance=220 package=THT]
  R8 = Resistor [tolerance=±5% power=0.25W resistance=220 package=THT]
  R9 = Resistor [tolerance=±5% power=0.25W resistance=220 package=THT]
  R10 = Resistor [tolerance=±5% power=0.25W resistance=220 package=THT]
  LED7 = LED - 5mm [color="Blue (470nm)" current=0.030A package="5 mm [THT]"]
  LED8 = LED - 5mm [color="Blue (470nm)" current=0.030A package="5 mm [THT]"]
  LED9 = LED - 5mm [color="Blue (470nm)" current=0.030A package="5 mm [THT]"]
  LED10 = LED - 5mm [color="Blue (470nm)" current=0.030A package="5 mm [THT]"]
  S1 = Pushbutton [package="[THT]"]
  S2 = Pushbutton [package="[THT]"]

nets:
  N1: A1.Pin_23, S2.Pin_1, S2.Pin_2
  N2: A1.Pin_24, LED5.anode
  N3: A1.Pin_26, LED3.anode
  N4: A1.Pin_27, HC-SR04_Sensor_1.TRIG
  N5: A1.Pin_28, HC-SR04_Sensor_1.ECHO
  N6: A1.Pin_30, LED1.anode
  N7: A1.Pin_31, LED2.anode
  N8: A1.Pin_33, LED4.anode
  N9: A1.Pin_37, S1.Pin_3, S1.Pin_4
  N10: HC-SR04_Sensor_1.VCC, S1.Pin_1, S1.Pin_2, S2.Pin_3, S2.Pin_4
  N11: HC-SR04_Sensor_1.GND, R1.Pin_0, R3.Pin_0, R4.Pin_0, R6.Pin_1, R7.Pin_1, R8.Pin_1, R9.Pin_1, R10.Pin_1
  N12: R6.Pin_0, LED6.cathode
  N13: R7.Pin_0, LED8.cathode
  N14: R8.Pin_0, LED7.cathode
  N15: R9.Pin_0, LED9.cathode
  N16: R10.Pin_0, LED10.cathode

notes:
  ↑LEDの部分は分かりづらいですがこうなってます．

custom parts:
  ESP32 DevKitc V4: ESP32-DevKitC board with ESP32-WROOM-32 module. ESP32-DevKitC V4 is a small-sized ESP32-based development board produced by Espressif. Most of the pins on the ESP module are broken out to the pin headers on the board. The pins D0, D1, D2, D3, CMD and CLK are used internally for communication between ESP32 and SPI flash memory. They are grouped on both sides near the USB connector. Avoid using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
