# Fritzing sketch unknown_sensor (saved by Fritzing 1.0.5)
breadboards: 1

parts:
  S1 = Pushbutton [package="[THT]"]
  S2 = Pushbutton [package="[THT]"]
  LED1 = RGB LED (com. cathode, rgb) [color="Red (633nm)" current=0.030A package="5 mm [THT]"]
  A1 = ESP32 DevKitc V4
  R1 = Resistor [tolerance=±5% power=0.25W resistance=220 package=THT]
  S3 = Tilt Switch [package=THT]

nets:
  N1: S1.Pin_1, S1.Pin_2, A1.Pin_23
  N2: S1.Pin_3, S1.Pin_4, S2.Pin_1, S2.Pin_2, A1.Pin_1, S3.Pin_1
  N3: S2.Pin_3, S2.Pin_4, A1.Pin_37
  N4: LED1.red_anode, A1.Pin_30
  N5: LED1.common_cathode, A1.Pin_31
  N6: LED1.green_anode, R1.Pin_1
  N7: A1.Pin_14, A1.Pin_32, A1.Pin_38, R1.Pin_0
  N8: A1.Pin_28, S3.Pin_2

notes:
  ↑謎のセンサ(?)
  ↓LED
  ←タクトスイッチ

custom parts:
  ESP32 DevKitc V4: ESP32-DevKitC board with ESP32-WROOM-32 module. ESP32-DevKitC V4 is a small-sized ESP32-based development board produced by Espressif. Most of the pins on the ESP module are broken out to the pin headers on the board. The pins D0, D1, D2, D3, CMD and CLK are used internally for communication between ESP32 and SPI flash memory. They are grouped on both sides near the USB connector. Avoid using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
